# Fritzing sketch cable_connection (saved by Fritzing 0.9.3b)
circuit board: 8.46667cm x 5.64444cm
breadboards: 1

parts:
  Part1 = Arduino Uno (Rev3)
  HC-SR04_Sensor_1 = HC-SR04 Ultrasonic Distance Sensor
  HC-SR04_Sensor_2 = HC-SR04 Ultrasonic Distance Sensor
  M1 = fc-51 [package=THT]
  M2 = fc-51 [package=THT]
  LED1 = smd LED [color="Red (633nm)" package="1206 [SMD]"]
  LED2 = smd LED [color="Red (633nm)" package="1206 [SMD]"]
  LED3 = smd LED [color="Green (555nm)" package="1206 [SMD]"]
  LED4 = smd LED [color="Green (555nm)" package="1206 [SMD]"]
  J1 = Basic Servo
  J2 = Basic Servo
  R1 = Resistor [tolerance=±5% resistance=470 package=THT]
  R2 = Resistor [tolerance=±5% resistance=100 package=THT]
  EDGY_motor_control1 = EDGY
  M3 = DC Motor
  M4 = DC Motor

nets:
  N1: Part1.A0, M1.pin1
  N2: Part1.A1, M2.pin1
  N3: Part1.D8, J1.pulse
  N4: Part1.D9_PWM, J2.pulse
  N5: Part1.D10_PWM/SS, LED3.anode, LED4.anode
  N6: Part1.D11_PWM/MOSI, LED1.anode, LED2.anode
  N7: Part1.D12/MISO, HC-SR04_Sensor_1.ECHO
  N8: Part1.D13/SCK, HC-SR04_Sensor_1.TRIG
  N9: Part1.D2, EDGY_motor_control1.B2
  N10: Part1.D3_PWM, EDGY_motor_control1.A2
  N11: Part1.D4, EDGY_motor_control1.B1
  N12: Part1.D5_PWM, EDGY_motor_control1.A1
  N13: Part1.D6_PWM, HC-SR04_Sensor_2.ECHO
  N14: Part1.D7, HC-SR04_Sensor_2.TRIG
  VCC: Part1.5V, HC-SR04_Sensor_1.VCC, HC-SR04_Sensor_2.VCC, M1.pin3, M2.pin3, J1.vcc, J2.vcc, EDGY_motor_control1.5V+
  GND: Part1.GND, HC-SR04_Sensor_1.GND, HC-SR04_Sensor_2.GND, M1.pin2, M2.pin2, J1.gnd, J2.gnd, R1.Pin_0, R2.Pin_0, EDGY_motor_control1.GND
  N15: LED1.cathode, LED2.cathode, R2.Pin_1
  N16: LED3.cathode, LED4.cathode, R1.Pin_1
  N17: EDGY_motor_control1.B2out, M4.pin_2
  N18: EDGY_motor_control1.A2out, M4.pin_1
  N19: EDGY_motor_control1.B1out, M3.pin_2
  N20: EDGY_motor_control1.A1out, M3.pin_1
